# Fritzing sketch EAS-BOT 1.0(PCB PRINT) (saved by Fritzing 0.9.3b)
circuit board: 15cm x 10cm
breadboards: 1

parts:
  HC-05_MAIN = Bluetooth HC-05 Macho
  RMOTOR = DC Motor  # not connected
  LMOTOR = DC Motor  # not connected
  LshoX = Basic Servo
  LarmY = Basic Servo
  LarmX = Basic Servo
  RarmX = Basic Servo
  RarmY = Basic Servo
  RshoX = Basic Servo
  RshoY = Basic Servo
  HC-05_PRIVATE = Bluetooth HC-05 Macho
  FLAME_SENSOR = KY-026
  RYEL1 = RGB LED (com. cathode, rbg) [package="5 mm [THT]"]
  LYEL1 = RGB LED (com. cathode, rbg) [package="5 mm [THT]"]
  HC_SWITCH = DIP SWITCH [package=dipswitch-02]
  MEGA_SWITCH = SWITCH-SPST-2 [package=switch-spst-vertical]
  LshoY = Basic Servo
  J5 = screw terminal, 3 pins
  J7 = screw terminal, 3 pins
  J12 = screw terminal, 3 pins
  J13 = screw terminal, 3 pins
  J14 = screw terminal, 3 pins
  J16 = screw terminal, 3 pins
  J20 = screw terminal, 3 pins
  L298N = H-Bridge with L298N  # not connected
  11_1V_PWR = screw terminal, 2 pins
  J22 = screw terminal, 3 pins
  J25 = screw terminal, 3 pins
  J24 = screw terminal, 3 pins
  J23 = screw terminal, 3 pins
  J6 = screw terminal, 3 pins
  J26 = screw terminal, 3 pins
  J27 = screw terminal, 3 pins
  J10 = screw terminal, 3 pins
  RMF = Basic Servo
  RTF = Basic Servo
  LPF = Basic Servo
  RPF = Basic Servo
  RIF = Basic Servo
  LRF = Basic Servo
  LMF = Basic Servo
  LTF = Basic Servo
  LIF = Basic Servo
  RRF = Basic Servo
  J28 = AVR ISP 6 Pin [package=2x3-ns]
  J29 = AVR ISP 6 Pin [package=2x3-ns]
  J30 = AVR ISP 6 Pin [package=2x3-ns]
  J31 = AVR ISP 6 Pin [package=2x3-ns]
  J32 = AVR ISP 6 Pin [package=2x3-ns]
  J33 = AVR ISP 6 Pin [package=2x3-ns]
  J34 = AVR ISP 6 Pin [package=2x3-ns]
  J35 = AVR ISP 6 Pin [package=2x3-ns]
  J36 = AVR ISP 6 Pin [package=2x3-ns]
  J37 = AVR ISP 6 Pin [package=2x3-ns]
  J39 = AVR ISP 6 Pin [package=2x3-ns]
  J40 = AVR ISP 6 Pin [package=2x3-ns]
  J42 = AVR ISP 6 Pin [package=2x3-ns]
  J44 = AVR ISP 6 Pin [package=2x3-ns]
  J58 = AVR ISP 6 Pin [package=2x3-ns]
  J59 = AVR ISP 6 Pin [package=2x3-ns]
  J63 = AVR ISP 6 Pin [package=2x3-ns]
  J64 = AVR ISP 6 Pin [package=2x3-ns]
  J67 = AVR ISP 6 Pin [package=2x3-ns]
  J69 = AVR ISP 6 Pin [package=2x3-ns]
  J70 = AVR ISP 6 Pin [package=2x3-ns]
  J72 = AVR ISP 6 Pin [package=2x3-ns]
  6V_SWITCH = DIP SWITCH [package=dipswitch-02]
  J74 = screw terminal, 3 pins
  12V_SWITCH = DIP SWITCH [package=dipswitch-02]
  12V_PWR = Power Jack [package=power_jack_slot]
  JP1 = Header 1 [package=snap-male]  # not connected
  JP2 = Header 1 [package=snap-male]  # not connected
  JP3 = Header 1 [package=snap-male]  # not connected
  JP4 = Header 1 [package=snap-male]  # not connected
  J77 = AVR ISP 6 Pin [package=2x3-ns]
  J78 = AVR ISP 6 Pin [package=2x3-ns]
  J79 = AVR ISP 6 Pin [package=2x3-ns]
  J80 = AVR ISP 6 Pin [package=2x3-ns]
  J81 = AVR ISP 6 Pin [package=2x3-ns]
  J83 = AVR ISP 6 Pin [package=2x3-ns]
  $5-49 = Basic Servo
  $2-43 = Basic Servo
  $6-51 = Basic Servo
  $1-41 = Basic Servo
  HEADY = Basic Servo
  $3-45 = Basic Servo
  $4-47 = Basic Servo
  $7-53 = Basic Servo
  J84 = AVR ISP 6 Pin [package=2x3-ns]
  LED3 = LED - 3mm [color="Blue (505nm)" package="3 mm [THT]"]
  R1 = Resistor [tolerance=±5% resistance=4.7 package=THT]
  Arduino_Mega = Arduino Mega 2560 (Rev3)
  J82 = AVR ISP 6 Pin [package=2x3-ns]
  EYES = RGB LED (com. cathode, rbg) [package="5 mm [THT]"]
  LYEL = LED - 3mm [color="Red (633nm)" package="3 mm [THT]"]
  EYESB = LED - 3mm [color="Red (633nm)" package="3 mm [THT]"]
  RYEL = LED - 3mm [color="Red (633nm)" package="3 mm [THT]"]
  REDLED = LED - 3mm [color="Red (633nm)" package="3 mm [THT]"]
  EYESG = LED - 3mm [color="Red (633nm)" package="3 mm [THT]"]
  R2 = Resistor [tolerance=±5% resistance=220 package=THT]
  R3 = Resistor [tolerance=±5% resistance=220 package=THT]
  R4 = Resistor [tolerance=±5% resistance=220 package=THT]
  R5 = Resistor [tolerance=±5% resistance=220 package=THT]
  R6 = Resistor [tolerance=±5% resistance=220 package=THT]
  R7 = Resistor [tolerance=±5% resistance=220 package=THT]
  WHITE = LED - 3mm [color="Red (633nm)" package="3 mm [THT]"]
  J85 = AVR ISP 6 Pin [package=2x3-ns]
  J87 = AVR ISP 6 Pin [package=2x3-ns]
  J88 = AVR ISP 6 Pin [package=2x3-ns]
  J89 = AVR ISP 6 Pin [package=2x3-ns]
  BACK_HC-SR04 = SRF05 Ultrasonic Rangefinder
  FRONT_HC-SR04 = SRF05 Ultrasonic Rangefinder
  JP5 = Header 6 [package=1x06-smd]  # not connected
  JP6 = Header 4 [package=molex-1x4_lock]
  JP7 = Header 4 [package=molex-1x4_lock]  # not connected
  JP8 = Header 2 [package=molex-1x2_lock]
  JP9 = Header 4 [package=molex-1x4_lock]  # not connected
  JP10 = Header 4 [package=molex-1x4_lock]
  JP11 = Header 2 [package=molex-1x2_lock]
  HEADX = Basic Servo
  U2 = LM2596 step down module
  U1 = LIPO-2000mAh [package=lipo-2000]  # not connected

nets (from the pcb view):
  N1: HC-05_MAIN.State, HC-05_PRIVATE.State, J87.1, J87.2
  N2: HC-05_MAIN.TXD, HC-05_PRIVATE.TXD, Arduino_Mega.D0_RX0, J87.5, J87.6
  N3: HC-05_MAIN.RXD, HC-05_PRIVATE.RXD, Arduino_Mega.D1_TX0, J87.3, J87.4
  VCC: HC-05_MAIN.VCC, HC-05_PRIVATE.VCC, HC_SWITCH.1, HC_SWITCH.2, J26.pin1, J26.pin2, J26.pin3, J27.pin1, J27.pin2, J27.pin3, J39.1, J39.2, J69.5, J69.6, J74.pin1, J74.pin2, J74.pin3, 12V_SWITCH.3, J81.1, J81.2, Arduino_Mega.5V, J88.3, J88.4, J89.1, J89.2, JP6.4, JP8.1, JP11.1
  N4: HC-05_MAIN.Key, HC-05_PRIVATE.Key, J88.5, J88.6
  N5: HC-05_MAIN.GND, HC_SWITCH.3
  N6: LshoX.pulse, J33.1, J33.2, J35.1, J35.2
  N7: LarmY.pulse, J33.5, J33.6, J35.5, J35.6, Arduino_Mega.D18/TX1
  N8: LarmX.pulse, J32.3, J32.4, J34.3, J34.4, Arduino_Mega.D20/SDA, Arduino_Mega.SDA, J85.3, J85.4
  GND: RarmX.gnd, RarmY.gnd, RshoX.gnd, RshoY.gnd, FLAME_SENSOR.pin2, LshoY.gnd, J22.pin1, J22.pin2, J22.pin3, J25.pin1, J25.pin2, J25.pin3, J24.pin1, J24.pin2, J24.pin3, J23.pin1, J23.pin2, J23.pin3, 6V_SWITCH.1, BACK_HC-SR04.GND, FRONT_HC-SR04.GND
  VCC_2: RarmX.vcc, RarmY.vcc, RshoX.vcc, RshoY.vcc, RMF.vcc, RTF.vcc, LPF.vcc, RPF.vcc, RIF.vcc, LRF.vcc, LMF.vcc, LTF.vcc, LIF.vcc, RRF.vcc
  N9: RarmX.pulse, J32.5, J32.6, J34.5, J34.6, Arduino_Mega.D21/SCL, Arduino_Mega.SCL, J85.1, J85.2
  N10: RarmY.pulse, J32.1, J32.2, J34.1, J34.2, Arduino_Mega.D19/RX1
  N11: RshoX.pulse, J33.3, J33.4, J35.3, J35.4
  N12: RshoY.pulse, J36.3, J36.4, J37.3, J37.4, Arduino_Mega.D15/RX3
  N13: HC-05_PRIVATE.GND, HC_SWITCH.4, J88.1, J88.2
  N14: FLAME_SENSOR.pin1, J80.5, J80.6, Arduino_Mega.A0
  VCC_3: FLAME_SENSOR.pin3, BACK_HC-SR04.VCC, FRONT_HC-SR04.VCC
  N15: RYEL1.red_anode, RYEL1.green_anode, RYEL.anode, R3.Pin_1
  GND_2: RYEL1.common_cathode, LYEL1.common_cathode, 11_1V_PWR.pin2, J67.1, J67.2, 6V_SWITCH.4, 12V_SWITCH.2, 12V_PWR.GNDBREAK, 12V_PWR.GND, $5-49.gnd, $2-43.gnd, $6-51.gnd, $1-41.gnd, HEADY.gnd, $3-45.gnd, $4-47.gnd, $7-53.gnd, Arduino_Mega.GND, EYES.common_cathode, LYEL.cathode, EYESB.cathode, RYEL.cathode, REDLED.cathode, EYESG.cathode, WHITE.cathode, J85.5, J85.6, J89.3, J89.4, HEADX.gnd, U2.IN-, U2.OUT-
  N16: LYEL1.red_anode, LYEL1.green_anode, LYEL.anode, R2.Pin_1
  N17: MEGA_SWITCH.O, 11_1V_PWR.pin1
  N18: MEGA_SWITCH.P, Arduino_Mega.VIN
  N19: LshoY.vcc, J12.pin1, J12.pin2, J12.pin3, J13.pin1, J13.pin2, J13.pin3, J14.pin1, J14.pin2, J14.pin3, J16.pin1, J16.pin2, J16.pin3, J20.pin1, J20.pin2, J20.pin3, J10.pin1, J10.pin2, J10.pin3, 6V_SWITCH.2
  N20: LshoY.pulse, J36.1, J36.2, J37.1, J37.2, Arduino_Mega.D14/TX3
  N21: J5.pin1, J5.pin2, J5.pin3, J7.pin1, J7.pin2, J7.pin3, J6.pin1, J6.pin2, J6.pin3, 12V_SWITCH.4, J89.5, J89.6, JP8.2, JP11.2
  GND_3: RMF.gnd, RTF.gnd, LPF.gnd, RPF.gnd, RIF.gnd, LRF.gnd, LMF.gnd, LTF.gnd, LIF.gnd, RRF.gnd
  N22: RMF.pulse, J40.3, J40.4, Arduino_Mega.D28
  N23: RTF.pulse, J39.5, J39.6, Arduino_Mega.D24
  N24: LPF.pulse, J58.1, J58.2
  N25: RPF.pulse, J42.3, J42.4, Arduino_Mega.D34
  N26: RIF.pulse, J40.1, J40.2, Arduino_Mega.D26
  N27: LRF.pulse, J59.5, J59.6, Arduino_Mega.D48
  N28: LMF.pulse, J59.3, J59.4, Arduino_Mega.D46
  N29: LTF.pulse, J44.5, J44.6, Arduino_Mega.D42
  N30: LIF.pulse, J59.1, J59.2, Arduino_Mega.D44
  N31: RRF.pulse, J40.5, J40.6, Arduino_Mega.D30
  N32: J28.1, J28.2, J29.1, J29.2
  N33: J28.3, J28.4, J29.3, J29.4
  N34: J28.5, J28.6, J29.5, J29.6
  N35: J30.2, J31.1, J31.2
  N36: J30.4, J31.3, J31.4
  N37: J30.6, J31.5, J31.6
  N38: J36.5, J36.6, J37.5, J37.6
  N39: J39.3, J39.4, Arduino_Mega.D22
  N40: J42.1, J42.2, Arduino_Mega.D32
  N41: J42.5, J42.6, Arduino_Mega.D36
  N42: J44.1, J44.2, Arduino_Mega.D38
  N43: J44.3, J44.4, Arduino_Mega.D40
  N44: J58.3, J58.4, R1.Pin_1, Arduino_Mega.D52
  N45: J58.5, J58.6, LED3.cathode
  N46: J63.1, J63.2, $2-43.pulse, Arduino_Mega.D43
  N47: J63.3, J63.4, $1-41.pulse, Arduino_Mega.D41
  N48: J63.5, J63.6, HEADY.pulse, Arduino_Mega.D39
  N49: J64.1, J64.2, Arduino_Mega.D37, HEADX.pulse
  N50: J64.3, J64.4, Arduino_Mega.D35, JP10.4
  N51: J64.5, J64.6, Arduino_Mega.D33, JP10.3
  N52: J67.3, J67.4, $7-53.pulse
  N53: J67.5, J67.6, $6-51.pulse
  N54: J69.1, J69.2, Arduino_Mega.D25, JP6.2
  N55: J69.3, J69.4, Arduino_Mega.D23, JP6.3
  N56: J70.1, J70.2, $5-49.pulse, Arduino_Mega.D49
  N57: J70.3, J70.4, $4-47.pulse, Arduino_Mega.D47
  N58: J70.5, J70.6, $3-45.pulse, Arduino_Mega.D45
  N59: J72.1, J72.2, Arduino_Mega.D31, JP10.2
  N60: J72.3, J72.4, Arduino_Mega.D29, JP10.1
  N61: J72.5, J72.6, Arduino_Mega.D27, JP6.1
  N62: 6V_SWITCH.3, U2.OUT+
  N63: 12V_SWITCH.1, 12V_PWR.PWR, U2.IN+
  N64: J77.1, J77.2, Arduino_Mega.A13
  N65: J77.3, J77.4, Arduino_Mega.A12
  N66: J77.5, J77.6, Arduino_Mega.A11
  N67: J78.1, J78.2, Arduino_Mega.A10
  N68: J78.3, J78.4, Arduino_Mega.A9
  N69: J78.5, J78.6, Arduino_Mega.A8
  N70: J79.1, J79.2, J84.5, J84.6, Arduino_Mega.A5
  N71: J79.3, J79.4, Arduino_Mega.A4, BACK_HC-SR04.Echo
  N72: J79.5, J79.6, Arduino_Mega.A3, BACK_HC-SR04.Trig
  N73: J80.1, J80.2, Arduino_Mega.A2, FRONT_HC-SR04.Trig
  N74: J80.3, J80.4, Arduino_Mega.A1, FRONT_HC-SR04.Echo
  N75: J81.3, J81.4, Arduino_Mega.3V3
  N76: J81.5, J81.6, Arduino_Mega.RESET
  N77: J83.1, J83.2, Arduino_Mega.D10_PWM, R4.Pin_0
  N78: J83.3, J83.4, Arduino_Mega.D9_PWM, R5.Pin_0
  N79: J83.5, J83.6, Arduino_Mega.D8_PWM, R6.Pin_0
  VCC_4: $5-49.vcc, $2-43.vcc, $6-51.vcc, $1-41.vcc, HEADY.vcc, $3-45.vcc, $4-47.vcc, $7-53.vcc, HEADX.vcc
  N80: J84.1, J84.2, Arduino_Mega.A7
  N81: J84.3, J84.4, Arduino_Mega.A6
  N82: LED3.anode, R1.Pin_0
  N83: Arduino_Mega.D13_PWM, J82.1, J82.2, R7.Pin_0
  N84: Arduino_Mega.D12_PWM, J82.3, J82.4, R3.Pin_0
  N85: Arduino_Mega.D11_PWM, J82.5, J82.6, R2.Pin_0
  N86: EYES.blue_anode, EYESB.anode, R4.Pin_1
  N87: EYES.green_anode, EYESG.anode, R5.Pin_1
  N88: REDLED.anode, R7.Pin_1
  N89: R6.Pin_1, WHITE.anode

custom parts:
  KY-026: ky-026 flame sensor module
  H-Bridge with L298N: h-bridge
  Header 6: Header 6 Standard 6-pin 0.1 header. Use with straight break away headers (SKU : PRT-00116), right angle break away headers (PRT-00553), swiss pins (PRT-00743), machine pins (PRT-00117), and female headers (PRT-00115). Molex polarized connector foot print use with SKU : PRT-08094 with associated crimp pins and housings. NOTES ON THE VARIANTS LOCK and LOCK_LONGPADS... This footprint was designed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
  LM2596 step down module: LM2596 DC-DC step down power supply module 3 A.
