# Fritzing sketch EAS-BOT 1.0 (saved by Fritzing 0.9.3b)
circuit board: 15cm x 10cm
breadboards: 1

parts:
  HC-05_MEGA = Bluetooth HC-05 Macho
  REDLED = smd LED [color="Red (633nm)" package="0805 [SMD]"]
  RMOTOR = DC Motor
  LMOTOR = DC Motor
  L_SHOULDER_X = Basic Servo
  L_ARM_Y = Basic Servo
  L_ARM_X = Basic Servo
  R_ARM_X = Basic Servo
  R_ARM_Y = Basic Servo
  R_SHOULDER_X = Basic Servo
  R_HAND = Basic Servo  # not connected
  L_HAND = Basic Servo  # not connected
  R_SHOULDER_Y = Basic Servo
  HC-05_NANO = Bluetooth HC-05 Macho
  S1 = KY-026
  LEFTRGB = RGB LED (com. cathode, rbg) [package="5 mm [THT]"]
  RIGHTRGB = RGB LED (com. cathode, rbg) [package="5 mm [THT]"]
  SW1 = DIP SWITCH [package=dipswitch-02]
  U2 = SWITCH-SPST-2 [package=switch-spst-vertical]
  U3 = SWITCH-SPST-2 [package=switch-spst-vertical]
  GREENRGB = RGB LED (com. cathode, rbg) [package="5 mm [THT]"]
  Arduino_Mega = Arduino Mega ADK (Rev3)
  L_SHOULDER_Y = Basic Servo
  Arduino_Nano = Arduino Nano (Rev3.0) (ICSP)
  LED1 = smd LED [color="White (4500K)" package="1206 [SMD]"]
  LED2 = smd LED [color="White (4500K)" package="1206 [SMD]"]
  J5 = screw terminal, 3 pins
  J7 = screw terminal, 3 pins  # not connected
  J9 = screw terminal, 3 pins
  J12 = screw terminal, 3 pins
  J13 = screw terminal, 3 pins
  J14 = screw terminal, 3 pins
  J15 = screw terminal, 3 pins  # not connected
  J16 = screw terminal, 3 pins
  J17 = screw terminal, 3 pins
  J18 = screw terminal, 3 pins  # not connected
  J20 = screw terminal, 3 pins
  L298N = H-Bridge with L298N
  U1 = LIPO-2000mAh [package=lipo-2000]
  J11 = screw terminal, 2 pins
  J21 = screw terminal, 3 pins  # not connected
  J22 = screw terminal, 3 pins  # not connected
  J25 = screw terminal, 3 pins  # not connected
  J24 = screw terminal, 3 pins  # not connected
  J23 = screw terminal, 3 pins  # not connected
  J6 = screw terminal, 3 pins
  J26 = screw terminal, 3 pins  # not connected
  J27 = screw terminal, 3 pins
  J10 = screw terminal, 3 pins
  RF3 = Basic Servo  # not connected
  RF1 = Basic Servo
  LF1 = Basic Servo  # not connected
  RF5 = Basic Servo  # not connected
  RF2 = Basic Servo
  LF2 = Basic Servo  # not connected
  LF3 = Basic Servo  # not connected
  LF5 = Basic Servo  # not connected
  LF4 = Basic Servo  # not connected
  RF4 = Basic Servo  # not connected
  J28 = AVR ISP 6 Pin [package=2x3-ns]
  J29 = AVR ISP 6 Pin [package=2x3-ns]
  J30 = AVR ISP 6 Pin [package=2x3-ns]
  J31 = AVR ISP 6 Pin [package=2x3-ns]
  J8 = screw terminal, 3 pins

nets:
  N1: HC-05_MEGA.TXD, Arduino_Mega.D0/RX0
  N2: HC-05_MEGA.RXD, Arduino_Mega.D1/TX0
  5V: HC-05_MEGA.VCC, Arduino_Mega.5V, J5.pin1, J5.pin2, J5.pin3, L298N.5V, J6.pin1, J6.pin2, J6.pin3
  N3: HC-05_MEGA.GND, SW1.3
  N4: REDLED.cathode, LEFTRGB.common_cathode, RIGHTRGB.common_cathode, LED1.cathode
  N5: REDLED.anode, Arduino_Mega.D11_PWM
  N6: RMOTOR.pin_1, L298N.M2-02
  N7: RMOTOR.pin_2, L298N.M2-01
  N8: LMOTOR.pin_1, L298N.M1-02
  N9: LMOTOR.pin_2, L298N.M1-01
  GND: L_SHOULDER_X.gnd, L_ARM_Y.gnd, L_ARM_X.gnd, R_ARM_X.gnd, R_ARM_Y.gnd, R_SHOULDER_X.gnd, R_SHOULDER_Y.gnd, S1.pin2, SW1.1, SW1.2, Arduino_Mega.GND, L_SHOULDER_Y.gnd, Arduino_Nano.GND, L298N.GND, U1.-, J11.pin2, J27.pin3
  VCC: L_SHOULDER_X.vcc, L_ARM_Y.vcc, L_ARM_X.vcc, R_ARM_X.vcc, R_ARM_Y.vcc, R_SHOULDER_X.vcc, R_SHOULDER_Y.vcc, U2.O, U3.O, L_SHOULDER_Y.vcc, J9.pin1, J9.pin2, J9.pin3, J12.pin1, J12.pin2, J12.pin3, J13.pin1, J13.pin2, J13.pin3, J14.pin1, J14.pin2, J14.pin3, J16.pin1, J16.pin2, J16.pin3, J17.pin1, J17.pin2, J17.pin3, J20.pin1, J20.pin2, J20.pin3, L298N.12V, U1.+, J11.pin1, J10.pin1, J10.pin2, J10.pin3, J8.pin1, J8.pin2, J8.pin3
  N10: L_SHOULDER_X.pulse, Arduino_Mega.D16/TX2
  N11: L_ARM_Y.pulse, Arduino_Mega.D18/TX1
  N12: L_ARM_X.pulse, Arduino_Mega.D20/SDA
  N13: R_ARM_X.pulse, Arduino_Mega.D21/SCL
  N14: R_ARM_Y.pulse, Arduino_Mega.D19/RX1
  N15: R_SHOULDER_X.pulse, Arduino_Mega.D17/RX2
  N16: R_SHOULDER_Y.pulse, Arduino_Mega.D15/RX3
  N17: HC-05_NANO.TXD, Arduino_Nano.D0/RX
  N18: HC-05_NANO.RXD, Arduino_Nano.D1/TX
  VCC_2: HC-05_NANO.VCC, Arduino_Nano.AREF, Arduino_Nano.3V3
  N19: HC-05_NANO.GND, SW1.4
  N20: S1.pin1, Arduino_Mega.A0, Arduino_Nano.A0
  N21: S1.pin3, Arduino_Nano.5V
  N22: S1.pin4, Arduino_Nano.A1
  N23: LEFTRGB.red_anode, LEFTRGB.green_anode, Arduino_Mega.D13_PWM
  N24: RIGHTRGB.red_anode, RIGHTRGB.green_anode, Arduino_Mega.D12_PWM
  N25: U2.P, Arduino_Nano.VIN
  N26: U3.P, Arduino_Mega.VIN
  N27: GREENRGB.red_anode, GREENRGB.green_anode, Arduino_Mega.D9_PWM
  N28: GREENRGB.common_cathode, LED2.cathode
  N29: Arduino_Mega.D14/TX3, L_SHOULDER_Y.pulse
  N30: Arduino_Mega.D10_PWM, LED1.anode
  N31: Arduino_Mega.D8_PWM, LED2.anode
  N32: Arduino_Mega.D2_PWM, L298N.ENB
  N33: Arduino_Mega.D3_PWM, L298N.IN4
  N34: Arduino_Mega.D4_PWM, L298N.IN3
  N35: Arduino_Mega.D5_PWM, L298N.IN2
  N36: Arduino_Mega.D6_PWM, L298N.IN1
  N37: Arduino_Mega.D7_PWM, L298N.ENA
  N38: Arduino_Mega.D22, RF1.pulse
  N39: Arduino_Mega.D24, RF2.pulse
  N40: J28.1, J28.2, J29.1, J29.2
  N41: J28.3, J28.4, J29.3, J29.4
  N42: J28.5, J28.6, J29.5, J29.6
  N43: J30.2, J31.1, J31.2
  N44: J30.4, J31.3, J31.4
  N45: J30.6, J31.5, J31.6

custom parts:
  KY-026: ky-026 flame sensor module
  H-Bridge with L298N: h-bridge
